# Fritzing sketch circuits (saved by Fritzing 0.9.9b)
circuit board: 8.46667cm x 5.64444cm
circuit board: 2cm x 1.5cm
circuit board: 2cm x 1.5cm
circuit board: 2cm x 1.5cm
breadboards: 4

parts:
  Raspberry_Pi_1 = Raspberry Pi 3 [part_number=RPI-3-V1.2]
  ADC1 = MCP3008 [package=dil16]
  R1 = TRIMPOT [package=trimpot_pth_s3_lock]
  S1 = Momentary Switch [package=ksa_sealed_tac_switch]
  LED1 = RGB LED (com. cathode, rgb) [package="5 mm [THT]"]
  S5 = Momentary Switch [package=ksa_sealed_tac_switch]
  R4 = Resistor [tolerance=±5% resistance=220 package="0805 [SMD]"]
  R6 = Resistor [tolerance=±5% resistance=220 package="0805 [SMD]"]
  R8 = Resistor [tolerance=±5% resistance=220 package="0805 [SMD]"]
  R10 = Resistor [tolerance=±5% resistance=220 package="0805 [SMD]"]
  R12 = Resistor [tolerance=±5% resistance=220 package="0805 [SMD]"]
  R14 = Resistor [tolerance=±5% resistance=220 package="0805 [SMD]"]
  R15 = TRIMPOT [package=trimpot_pth_s3_lock]
  S6 = Momentary Switch [package=ksa_sealed_tac_switch]
  R16 = TRIMPOT [package=trimpot_pth_s3_lock]
  S7 = Momentary Switch [package=ksa_sealed_tac_switch]
  R17 = Resistor [tolerance=±5% power=0.25 resistance=1M package=THT]
  R18 = Resistor [tolerance=±5% power=0.25 resistance=1M package=THT]
  R19 = Resistor [tolerance=±5% power=0.25 resistance=1M package=THT]
  R20 = Resistor [tolerance=±5% power=0.25 resistance=1M package=THT]
  U1 = 74HC595 [package="DIP16 [THT]"]
  LED3 = RGB LED (com. cathode, rgb) [package="5 mm [THT]"]

nets (from the breadboard view):
  3V3: Raspberry_Pi_1.3v3, Raspberry_Pi_1.3V3, ADC1.VREF, ADC1.VDD, R1.CCW, R15.CCW, R16.CCW, U1.MR
  GND: Raspberry_Pi_1.GND, ADC1.DGND, ADC1.AGND, R1.CW, LED1.common_cathode, S5.3, R15.CW, R16.CW, R17.Pin_0, R18.Pin_0, R19.Pin_0, R20.Pin_0, U1.GND, LED3.common_cathode
  N1: Raspberry_Pi_1.GPIO17, U1.ST_CP
  N2: Raspberry_Pi_1.GPIO27, U1.OE
  N3: Raspberry_Pi_1.GPIO10, ADC1.Din, U1.DS
  N4: Raspberry_Pi_1.GPIO9, ADC1.Dout
  N5: Raspberry_Pi_1.GPIO11, ADC1.CLK, U1.SH_CP
  N6: Raspberry_Pi_1.GPIO5, ADC1.CS/SHDN
  N7: Raspberry_Pi_1.GPIO16, S5.1
  5V: Raspberry_Pi_1.5V, U1.VCC
  N8: ADC1.CH0, S1.1, S6.1, S7.1, R20.Pin_1
  N9: ADC1.CH1, R1.WIPER, S1.3, R19.Pin_1
  N10: ADC1.CH2, R15.WIPER, S6.3, R18.Pin_1
  N11: ADC1.CH3, R16.WIPER, S7.3, R17.Pin_1
  N12: LED1.red_anode, R4.Pin_0
  N13: LED1.green_anode, R6.Pin_0
  N14: LED1.blue_anode, R10.Pin_0
  N15: R4.Pin_1, U1.Q0
  N16: R6.Pin_1, U1.Q2
  N17: R8.Pin_0, LED3.red_anode
  N18: R8.Pin_1, U1.Q4
  N19: R10.Pin_1, U1.Q3
  N20: R12.Pin_0, LED3.blue_anode
  N21: R12.Pin_1, U1.Q6
  N22: R14.Pin_0, LED3.green_anode
  N23: R14.Pin_1, U1.Q5

notes:
  gnd
  3.3v
  d_btn
  d_seq
  pull-down
  resistors
